// Logisim project cpu.circ as structural Verilog: 6 circuits, main circuit alu
module alu (
  input  [7:0] A,
  input  write,
  input  clr,
  input  use_mem,
  input  in_5,
  input  [7:0] B,
  input  [2:0] opcode,
  output [7:0] out_8,
  output zero,
  output overflow,
  output overflow_2
);

  wire not_1_out, or_2_out;
  wire [7:0] adder_1_out, and_1_out, multiplexer_1_out, multiplexer_2_out, multiplexer_3_out, not_2_out,
       or_1_out, register_1_q, shifter_1_out, shifter_2_out, subtractor_1_out;

  Multiplexer #(.width(8)) multiplexer_1 (
    .in0(A), .in1(register_1_q), .out(multiplexer_1_out), .sel(use_mem));  // open: en
  Multiplexer #(.width(8)) multiplexer_2 (
    .in0(multiplexer_1_out), .in1(B), .out(multiplexer_2_out), .sel(in_5));  // open: en
  not not_1 (not_1_out, in_5);
  Multiplexer #(.width(8)) multiplexer_3 (
    .in0(multiplexer_1_out), .in1(B), .out(multiplexer_3_out), .sel(not_1_out));  // open: en
  Adder adder_1 (.a(multiplexer_3_out), .b(multiplexer_2_out), .out(adder_1_out), .cout(overflow));  // open: cin
  Subtractor subtractor_1 (
    .a(multiplexer_3_out), .b(multiplexer_2_out), .out(subtractor_1_out), .bout(overflow_2));  // open: bin
  Shifter #(.shift("lr")) shifter_1 (.in(multiplexer_2_out), .\dist (3'b001), .out(shifter_1_out));
  Shifter shifter_2 (.in(multiplexer_2_out), .\dist (3'b001), .out(shifter_2_out));
  assign or_1_out = multiplexer_3_out | multiplexer_2_out;  // OR_Gate or_1, 8 bits wide
  assign and_1_out = multiplexer_3_out & multiplexer_2_out;  // AND_Gate and_1, 8 bits wide
  assign not_2_out = ~multiplexer_2_out;  // NOT_Gate not_2, 8 bits wide
  Multiplexer #(.select(3), .width(8)) multiplexer_4 (
    .in0(multiplexer_2_out), .in1(adder_1_out), .in2(subtractor_1_out), .in3(shifter_1_out),
    .in4(shifter_2_out), .in5(or_1_out), .in6(and_1_out), .in7(not_2_out), .out(out_8), .sel(opcode));  // open: en
  Register register_1 (.D(out_8), .Q(register_1_q), .clk(write), .clr(clr));  // open: en
  or or_2 (or_2_out, out_8[0], out_8[1], out_8[2], out_8[3], out_8[5], out_8[6], out_8[7], out_8[4]);
  not not_3 (zero, or_2_out);
endmodule

module cpu (
  input  [7:0] in_1,
  input  in_2,
  input  in_3,
  output [7:0] out_4
);

  wire controller_1_out_3;
  wire [1:0] counter_1_q;
  wire [2:0] controller_1_opcode;
  wire [3:0] controller_1_address;
  wire [7:0] alu2_1_out_5, ram_1_data, ram_2_data;

  Clock clock_1 ();  // open: out
  Counter #(.width(2), .max('h3)) counter_1 (.Q(counter_1_q), .clk(in_3));  // open: load, D, count, carry, clr
  RAM #(.addrWidth(2), .bus("separate")) ram_1 (
    .addr(counter_1_q), .din(in_1), .data(ram_1_data), .clk(in_3));  // open: str, sel, ld, clr
  controller controller_1 (
    .in_1(ram_1_data), .opcode(controller_1_opcode), .address(controller_1_address),
    .out_3(controller_1_out_3));
  RAM #(.addrWidth(4), .bus("separate")) ram_2 (
    .addr(controller_1_address), .din(out_4), .data(ram_2_data), .str(controller_1_out_3), .clk(in_3));  // open: sel, ld, clr
  // Probe on ram_2_data
  // Probe on controller_1_opcode
  alu2 alu2_1 (
    .A(out_4), .in_2(in_2), .B(ram_2_data), .opcode(controller_1_opcode), .out_5(alu2_1_out_5));  // open: zero, overflow, overflow_2
  Register register_1 (.D(alu2_1_out_5), .Q(out_4), .clk(in_3));  // open: en, clr
endmodule

module alu2 (
  input  [7:0] A,
  input  in_2,
  input  [7:0] B,
  input  [2:0] opcode,
  output [7:0] out_5,
  output zero,
  output overflow,
  output overflow_2
);

  wire not_1_out, or_2_out;
  wire [7:0] adder_1_out, and_1_out, multiplexer_1_out, multiplexer_2_out, not_2_out, or_1_out,
       shifter_1_out, shifter_2_out, subtractor_1_out;

  Multiplexer #(.width(8)) multiplexer_1 (.in0(A), .in1(B), .out(multiplexer_1_out), .sel(in_2));  // open: en
  not not_1 (not_1_out, in_2);
  Multiplexer #(.width(8)) multiplexer_2 (.in0(A), .in1(B), .out(multiplexer_2_out), .sel(not_1_out));  // open: en
  Adder adder_1 (.a(multiplexer_2_out), .b(multiplexer_1_out), .out(adder_1_out), .cout(overflow));  // open: cin
  Subtractor subtractor_1 (
    .a(multiplexer_2_out), .b(multiplexer_1_out), .out(subtractor_1_out), .bout(overflow_2));  // open: bin
  Shifter #(.shift("lr")) shifter_1 (.in(multiplexer_1_out), .\dist (3'b001), .out(shifter_1_out));
  Shifter shifter_2 (.in(multiplexer_1_out), .\dist (3'b001), .out(shifter_2_out));
  assign or_1_out = multiplexer_2_out | multiplexer_1_out;  // OR_Gate or_1, 8 bits wide
  assign and_1_out = multiplexer_2_out & multiplexer_1_out;  // AND_Gate and_1, 8 bits wide
  assign not_2_out = ~multiplexer_1_out;  // NOT_Gate not_2, 8 bits wide
  Multiplexer #(.select(3), .width(8)) multiplexer_3 (
    .in0(multiplexer_1_out), .in1(adder_1_out), .in2(subtractor_1_out), .in3(shifter_1_out),
    .in4(shifter_2_out), .in5(or_1_out), .in6(and_1_out), .in7(not_2_out), .out(out_5), .sel(opcode));  // open: en
  or or_2 (or_2_out, out_5[0], out_5[1], out_5[2], out_5[3], out_5[5], out_5[6], out_5[7], out_5[4]);
  not not_3 (zero, or_2_out);
endmodule

module controller (
  input  [7:0] in_1,
  output [3:0] address,
  output out_3,
  output [2:0] opcode
);


  assign address = in_1[3:0];
  assign opcode = in_1[7:5];
  assign out_3 = in_1[4];
endmodule

module cpu2 (
  input  [7:0] in_1
);

  wire clock_1_out, controller2_1_alu, controller2_1_clear_mem, controller2_1_jump,
       controller2_1_write_from_alu, controller2_1_write_from_input, controller2_1_write_to_alu_reg,
       not_1_out, not_2_out, not_3_out, not_4_out, or_1_out;
  wire [2:0] controller2_1_alu_mem_opcode, multiplexer_2_out;
  wire [3:0] controller2_1_memory_address, counter_1_q;
  wire [7:0] alu2_1_out_5, multiplexer_1_out, ram_1_data, ram_2_data, register_1_q;

  not not_1 (not_1_out, controller2_1_jump);
  Counter #(.width(4), .max('hf)) counter_1 (
    .load(controller2_1_jump), .D(controller2_1_memory_address), .count(not_1_out), .Q(counter_1_q),
    .clk(clock_1_out));  // open: carry, clr
  Clock clock_1 (.out(clock_1_out));
  controller2 controller2_1 (
    .in_1(ram_1_data), .memory_address(controller2_1_memory_address),
    .alu_mem_opcode(controller2_1_alu_mem_opcode), .write_from_input(controller2_1_write_from_input),
    .alu(controller2_1_alu), .write_from_alu(controller2_1_write_from_alu),
    .clear_mem(controller2_1_clear_mem), .write_to_alu_reg(controller2_1_write_to_alu_reg),
    .jump(controller2_1_jump));
  RAM #(.addrWidth(4), .bus("separate")) ram_1 (
    .addr(counter_1_q), .din(ram_1_data), .data(ram_1_data), .clk(clock_1_out));  // open: str, sel, ld, clr
  not not_2 (not_2_out, controller2_1_write_from_input);
  Multiplexer #(.width(8)) multiplexer_1 (
    .in0(in_1), .in1(register_1_q), .out(multiplexer_1_out), .sel(not_2_out));  // open: en
  not not_3 (not_3_out, controller2_1_alu);
  // Probe on multiplexer_1_out
  Multiplexer #(.width(3)) multiplexer_2 (
    .in0(controller2_1_alu_mem_opcode), .in1(3'b000), .out(multiplexer_2_out), .sel(not_3_out));  // open: en
  or or_1 (or_1_out, controller2_1_write_from_input, controller2_1_write_from_alu);
  RAM #(.addrWidth(4), .bus("separate")) ram_2 (
    .addr(controller2_1_memory_address), .din(multiplexer_1_out), .data(ram_2_data), .str(or_1_out),
    .clk(clock_1_out), .clr(controller2_1_clear_mem));  // open: sel, ld
  not not_4 (not_4_out, controller2_1_write_to_alu_reg);
  // Probe on register_1_q
  alu2 alu2_1 (
    .A(ram_2_data), .in_2(not_4_out), .B(register_1_q), .opcode(multiplexer_2_out), .out_5(alu2_1_out_5));  // open: zero, overflow, overflow_2
  Register register_1 (.D(alu2_1_out_5), .Q(register_1_q), .clk(clock_1_out));  // open: en, clr
  // Probe on alu2_1_out_5
endmodule

module controller2 (
  input  [7:0] in_1,
  output [3:0] memory_address,
  output [2:0] alu_mem_opcode,
  output write_from_input,
  output alu,
  output write_from_alu,
  output clear_mem,
  output write_to_alu_reg,
  output jump
);

  wire [2:0] multiplexer_1_out, multiplexer_2_out, multiplexer_3_out, multiplexer_4_out, multiplexer_5_out;

  Multiplexer #(.width(3)) multiplexer_1 (
    .in0(in_1[6:4]), .in1(3'b000), .out(multiplexer_1_out), .sel(in_1[7]));  // open: en
  Multiplexer #(.width(3)) multiplexer_2 (
    .in0(in_1[6:4]), .in1(3'b000), .out(multiplexer_2_out), .sel(in_1[7]));  // open: en
  Multiplexer #(.width(3)) multiplexer_3 (
    .in0(in_1[6:4]), .in1(3'b000), .out(multiplexer_3_out), .sel(in_1[7]));  // open: en
  Multiplexer #(.width(3)) multiplexer_4 (
    .in0(in_1[6:4]), .in1(3'b000), .out(multiplexer_4_out), .sel(in_1[7]));  // open: en
  Multiplexer #(.width(3)) multiplexer_5 (
    .in0(in_1[6:4]), .in1(3'b000), .out(multiplexer_5_out), .sel(in_1[7]));  // open: en
  and and_1 (write_from_input, multiplexer_1_out[0], ~multiplexer_1_out[1], ~multiplexer_1_out[2]);  // AND_Gate
  and and_2 (write_from_alu, multiplexer_2_out[0], multiplexer_2_out[1], ~multiplexer_2_out[2]);  // AND_Gate
  and and_3 (clear_mem, multiplexer_3_out[0], multiplexer_3_out[1], multiplexer_3_out[2]);
  and and_4 (write_to_alu_reg, multiplexer_4_out[0], ~multiplexer_4_out[1], multiplexer_4_out[2]);  // AND_Gate
  and and_5 (jump, ~multiplexer_5_out[0], multiplexer_5_out[1], ~multiplexer_5_out[2]);  // AND_Gate
  Multiplexer #(.width(3)) multiplexer_6 (.in0(in_1[6:4]), .in1(3'b000), .out(alu_mem_opcode), .sel(jump));  // open: en

  assign alu = in_1[7];
  assign memory_address = in_1[3:0];
endmodule
